# Fritzing sketch marble_clock (saved by Fritzing 0.9.6b)
breadboards: 1

parts:
  Part1 = Arduino Nano (Rev3.0)
  Mod1 = TMC2209 [package=THT]
  J1 = Power Jack [package=power_jack_pth_lock]
  M1 = Stepper Motor - Bipolar

nets:
  GND: Part1.GND, Mod1.GND, Mod1.MS1, J1.GND
  N1: Part1.D4, Mod1.EN
  N2: Part1.D7, Mod1.Step
  N3: Part1.D8, Mod1.Dir
  N4: Part1.VIN, Mod1.VM, J1.PWR
  5V: Part1.5V, Mod1.VDD, Mod1.MS2
  N5: Mod1.B2, M1.C
  N6: Mod1.B1, M1.A
  N7: Mod1.A1, M1.B
  N8: Mod1.A2, M1.D

notes:
  12v

custom parts:
  TMC2209: TMC2209-LA stepper motor controller and driver. Supply voltage 4.75-28V Iphase up to 1.77A rms (2.5A peak)
